# Fritzing sketch Tricopter-v2 (saved by Fritzing 0.4.3b)
breadboards: 4

parts:
  J1 = female pin header, 6 pins [form="♂ (male)"]
  J1_2 = female pin header, 7 pins [form="♂ (male)"]
  J1_3 = female pin header, 7 pins [form="♂ (male)"]
  U1 = Voltage Regulator - 5V [package="TO220 [THT]"]
  U2 = Voltage Regulator - 3.3V [package="TO220 [THT]"]
  U3 = atmega168 [package="DIP28 [THT]"]
  C1 = Electrolytic Capacitor [package=THT]
  C2 = Electrolytic Capacitor [package=THT]
  C3 = Electrolytic Capacitor [package=THT]
  XTAL1 = Crystal [package=THT]
  C4 = Ceramic Capacitor [package=THT]
  C4_2 = Ceramic Capacitor [package=THT]
  R1 = Resistor [resistance=10k package=THT]
  J2 = female pin header, 8 pins [form="♀ (female)"]
  J2_2 = female pin header, 8 pins [form="♀ (female)"]
  J3 = female pin header, 3 pins [form="♀ (female)"]
  J3_2 = female pin header, 5 pins [form="♀ (female)"]

nets:
  N1: J1.pin1, U3.Pin_17
  N2: J1.pin2, U3.Pin_16
  N3: J1.pin3, U3.Pin_15
  N4: J1.pin4, U3.Pin_12
  N5: J1.pin5, U3.Pin_11
  N6: J1.pin6, U3.Pin_5
  GND: J1_2.pin1, J1_2.pin2, J1_2.pin3, J1_2.pin4, J1_2.pin5, J1_2.pin6, J1_2.pin7, U1.GND, U2.GND, U3.Pin_8, U3.Pin_22, C1.-, C2.-, C3.-, C4.pin_0, C4_2.pin_0, J2.pin2, J3.pin2, J3_2.pin4
  N7: J1_3.pin1, J1_3.pin2, J1_3.pin3, J1_3.pin4, J1_3.pin5, J1_3.pin6, J1_3.pin7, U1.input_voltage, C1.+
  5V: U1.output_voltage, U2.input_voltage, U3.Pin_7, U3.Pin_20, C2.+, R1.Pin_0, J3_2.pin5
  N8: U2.output_voltage, U3.Pin_21, C3.+, J2.pin1, J3.pin1
  N9: U3.Pin_1, R1.Pin_1, J3_2.pin1
  N10: U3.Pin_2, J3.pin3, J3_2.pin2
  N11: U3.Pin_3, J3_2.pin3
  N12: U3.Pin_9, XTAL1.pin_0, C4.pin_1
  N13: U3.Pin_10, XTAL1.pin_1, C4_2.pin_1
  N14: U3.Pin_23, J2.pin6
  N15: U3.Pin_24, J2.pin7
  N16: U3.Pin_25, J2.pin8
  N17: U3.Pin_26, J2_2.pin8
  N18: U3.Pin_27, J2_2.pin7
  N19: U3.Pin_28, J2_2.pin6

notes:
  Servo connection +6v
  Spectrum reciver satelite
  Arduino board (programming)
