# Fritzing sketch Tricopter-v3 (saved by Fritzing 0.4.3b)
breadboards: 1

parts:
  U1 = atmega168 [package="DIP28 [THT]"]
  6 = female pin header, 3 pins [form="♂ (male)"]
  5 = female pin header, 3 pins [form="♂ (male)"]
  3 = female pin header, 3 pins [form="♂ (male)"]
  9 = female pin header, 3 pins [form="♂ (male)"]
  10 = female pin header, 3 pins [form="♂ (male)"]
  11 = female pin header, 3 pins [form="♂ (male)"]
  txrxR = female pin header, 5 pins [form="♀ (female)"]

nets:
  N1: U1.Pin_1, txrxR.pin5
  N2: U1.Pin_2, txrxR.pin4
  N3: U1.Pin_3, txrxR.pin3
  N4: U1.Pin_5, 3.pin1
  N5: U1.Pin_8, U1.Pin_22
  N6: U1.Pin_11, 5.pin1
  N7: U1.Pin_12, 6.pin1
  N8: U1.Pin_15, 9.pin1
  N9: U1.Pin_16, 10.pin1
  N10: U1.Pin_17, 11.pin1
