# Fritzing sketch Tricopter (saved by Fritzing 0.4.3b)
breadboards: 2

parts:
  U1 = atmega168 [package="DIP28 [THT]"]
  Arduino1 = Arduino
  R1 = Resistor [resistance=10k package=THT]
  Power_plug1 = Power plug
  U2 = Voltage Regulator - 5V [package="TO220 [THT]"]
  XTAL1 = Crystal [package=THT]
  C1 = Ceramic Disk Capacitor [package=THT]
  C2 = Ceramic Capacitor [package=THT]
  J1 = female pin header, 3 pins [form="♀ (female)"]
  U3 = Voltage Regulator - 3.3V [package="TO220 [THT]"]
  R2 = Resistor [resistance=33k package=THT]
  J3 = female pin header, 4 pins [form="♀ (female)"]
  J3_2 = female pin header, 4 pins [form="♀ (female)"]
  R2_2 = Resistor [resistance=33k package=THT]
  R2_3 = Resistor [resistance=33k package=THT]
  C3 = Ceramic Capacitor [package=THT]
  C3_2 = Ceramic Capacitor [package=THT]
  C3_3 = Ceramic Capacitor [package=THT]
  C4 = Electrolytic Capacitor [package=THT]
  R3 = Resistor [resistance=1k package=THT]
  R3_2 = Resistor [resistance=1k package=THT]
  R3_3 = Resistor [resistance=1k package=THT]
  C4_2 = Electrolytic Capacitor [package=THT]
  C4_3 = Electrolytic Capacitor [package=THT]
  J4 = Basic Servo
  J4_2 = Basic Servo
  J4_3 = Basic Servo
  J4_4 = Basic Servo
  J2 = female pin header, 4 pins [form="♀ (female)"]

nets:
  N1: U1.Pin_1, Arduino1.RST, R1.Pin_0, J2.pin2
  N2: U1.Pin_2, Arduino1.D0RX, J1.pin1, J2.pin4
  N3: U1.Pin_3, Arduino1.D1TX, J2.pin3
  5V: U1.Pin_7, U1.Pin_20, R1.Pin_1, U2.output_voltage, J3_2.pin1, J4.vcc, J4_2.vcc, J4_3.vcc, J4_4.vcc
  GND: U1.Pin_8, U1.Pin_22, Arduino1.GND, Power_plug1.GND, U2.GND, C1.pin_1, C2.pin_1, J1.pin3, U3.GND, J3.pin1, C3.pin_1, C3_2.pin_0, C3_3.pin_1, C4.-, C4_2.-, C4_3.-, J4.gnd, J4_2.gnd, J4_3.gnd, J4_4.gnd, J2.pin1
  N4: U1.Pin_9, XTAL1.pin_0, C2.pin_0
  N5: U1.Pin_10, XTAL1.pin_1, C1.pin_0
  N6: U1.Pin_11, J4_4.pulse
  N7: U1.Pin_12, J4_3.pulse
  N8: U1.Pin_15, J4.pulse
  N9: U1.Pin_16, J4_2.pulse
  N10: U1.Pin_23, R3.Pin_0, C4_3.+
  N11: U1.Pin_24, C4.+, R3_2.Pin_1
  N12: U1.Pin_25, R3_3.Pin_1, C4_2.+
  N13: U1.Pin_26, R2.Pin_0, C3_3.pin_0
  N14: U1.Pin_27, R2_2.Pin_1, C3_2.pin_1
  N15: U1.Pin_28, R2_3.Pin_1, C3.pin_0
  N16: Power_plug1.VCC, U2.input_voltage, U3.input_voltage
  N17: J1.pin2, U3.output_voltage
  N18: R2.Pin_1, J3.pin2
  N19: J3.pin3, R2_2.Pin_0
  N20: J3.pin4, R2_3.Pin_0
  N21: J3_2.pin2, R3.Pin_1
  N22: J3_2.pin3, R3_2.Pin_0
  N23: J3_2.pin4, R3_3.Pin_0
